// Logisim project CARRY_LOOK_AHEAD.circ as structural Verilog: 2 circuits, main circuit main
module main (
  input  C0,
  input  X0,
  input  Y0,
  input  X1,
  input  Y1,
  input  X2,
  input  Y2,
  input  X3,
  input  Y3,
  output C1,
  output C2,
  output C3,
  output C4
);

  wire and_1_out, and_2_out, and_3_out, and_4_out, and_5_out, and_6_out, and_7_out, and_8_out, and_9_out,
       and_10_out, and_11_out, and_12_out, and_13_out, P3P2P1P0C0_out, xor_1_out, xor_2_out, xor_3_out,
       xor_4_out;
  wire [3:0] xor_5_out;

  Hex_Digit_Display X (.value({X3, X2, X1, X0}));  // open: dp
  Hex_Digit_Display Y (.value({Y3, Y2, Y1, Y0}));  // open: dp
  xor xor_1 (xor_1_out, X0, Y0);
  and and_1 (and_1_out, X0, Y0);
  xor xor_2 (xor_2_out, X1, Y1);
  and and_2 (and_2_out, X1, Y1);
  xor xor_3 (xor_3_out, X2, Y2);
  and and_3 (and_3_out, X2, Y2);
  xor xor_4 (xor_4_out, X3, Y3);
  and and_4 (and_4_out, X3, Y3);
  and and_5 (and_5_out, and_1_out, xor_2_out);
  and and_6 (and_6_out, and_2_out, xor_3_out);
  and and_7 (and_7_out, C0, xor_1_out);
  and and_8 (and_8_out, xor_2_out, and_1_out, xor_3_out);
  and and_9 (and_9_out, and_3_out, xor_4_out);
  and and_10 (and_10_out, xor_1_out, C0, xor_2_out);
  and and_11 (and_11_out, and_2_out, xor_3_out, xor_4_out);
  and and_12 (and_12_out, C0, xor_1_out, xor_2_out, xor_3_out);
  and and_13 (and_13_out, and_1_out, xor_2_out, xor_3_out, xor_4_out);
  or or_1 (C1, and_7_out, and_1_out);
  xor xor_5 (xor_5_out[0], xor_1_out, C0);
  xor xor_6 (xor_5_out[1], xor_2_out, C1);
  or or_2 (C2, and_5_out, and_10_out, and_2_out);
  or or_3 (C3, and_6_out, and_8_out, and_12_out, and_3_out);
  xor xor_7 (xor_5_out[2], xor_3_out, C2);
  or or_4 (C4, P3P2P1P0C0_out, and_13_out, and_11_out, and_9_out, and_4_out);
  xor xor_8 (xor_5_out[3], C3, xor_4_out);
  and P3P2P1P0C0 (P3P2P1P0C0_out, xor_1_out, xor_2_out, C0, xor_3_out, xor_4_out);
  Hex_Digit_Display hex_digit_display_1 (.value(xor_5_out));  // open: dp

  // Notes on the sheet:
  //   P0
endmodule

module TEST (
  input  C0,
  input  X0,
  input  P0,
  input  Y0,
  input  G0,
  input  X1,
  input  P1,
  input  Y1,
  input  G1,
  input  X2,
  input  P2,
  input  Y2,
  input  G2,
  input  X3,
  input  P3,
  input  Y3,
  input  G3,
  output C1,
  output C2,
  output C3,
  output C4
);

  wire and_5_out, and_6_out, and_7_out, and_8_out, and_9_out, and_10_out, and_11_out, and_12_out, and_13_out,
       P3P2P1P0C0_out;

  Hex_Digit_Display hex_digit_display_1 (.value({X3, X2, X1, X0}));  // open: dp
  Hex_Digit_Display hex_digit_display_2 (.value({Y3, Y2, Y1, Y0}));  // open: dp
  xor xor_1 (P0, X0, Y0);
  and and_1 (G0, X0, Y0);
  xor xor_2 (P1, X1, Y1);
  and and_2 (G1, X1, Y1);
  xor xor_3 (P2, X2, Y2);
  and and_3 (G2, X2, Y2);
  xor xor_4 (P3, X3, Y3);
  and and_4 (G3, X3, Y3);
  and and_5 (and_5_out, G0, P1);
  and and_6 (and_6_out, G1, P2);
  and and_7 (and_7_out, C0, P0);
  and and_8 (and_8_out, P1, G0, P2);
  and and_9 (and_9_out, G2, P3);
  and and_10 (and_10_out, P0, C0, P1);
  and and_11 (and_11_out, G1, P2, P3);
  and and_12 (and_12_out, C0, P0, P1, P2);
  and and_13 (and_13_out, G0, P1, P2, P3);
  or or_1 (C1, and_7_out, G0);
  or or_2 (C2, and_5_out, and_10_out, G1);
  or or_3 (C3, and_6_out, and_8_out, and_12_out, G2);
  or or_4 (C4, P3P2P1P0C0_out, and_13_out, and_11_out, and_9_out, G3);
  and P3P2P1P0C0 (P3P2P1P0C0_out, P0, P1, C0, P2, P3);
endmodule
